# Fritzing sketch yl-39 (saved by Fritzing 0.9.2b)

parts:
  Part1 = Arduino Uno (Rev3)
  JP1 = Header 4 [package=screwterminal-3.5mm-4_lock]

nets:
  N1: Part1.A1, JP1.4
  N2: Part1.GND, JP1.2
  N3: Part1.D6_PWM, JP1.1

notes:
  YL-39 Pins (from top to bottom)
  1. VCC
  2. GND
  3. D0
  4. A0
