# Fritzing sketch HHV1701 (saved by Fritzing 0.9.3b)

parts:
  Part1 = MEGA2560v3ProtoShield
  J1 = Dagu DGServo 9g header (male) [package=THT]  # not connected
  JP3 = Header 4 [package=molex-1x4_lock]
  J3 = Dagu DGServo 9g header (male) [package=THT]
  J4 = Dagu DGServo 9g header (male) [package=THT]
  J5 = Dagu DGServo 9g header (male) [package=THT]
  J6 = Dagu DGServo 9g header (male) [package=THT]
  J7 = Dagu DGServo 9g header (male) [package=THT]
  J8 = Dagu DGServo 9g header (male) [package=THT]
  J9 = Dagu DGServo 9g header (male) [package=THT]
  J10 = Dagu DGServo 9g header (male) [package=THT]
  J11 = Dagu DGServo 9g header (male) [package=THT]
  J12 = Dagu DGServo 9g header (male) [package=THT]
  J13 = Dagu DGServo 9g header (male) [package=THT]
  J14 = Dagu DGServo 9g header (male) [package=THT]
  J15 = Dagu DGServo 9g header (male) [package=THT]

nets:
  N1: Part1.N$27, J15.gnd
  N2: Part1.N$34, J15.Vcc
  N3: Part1.N$35, J15.pulse
  N4: Part1.N$51, JP3.3
  N5: Part1.N$52, JP3.2
  N6: Part1.N$53, JP3.1
  N7: Part1.N$56, JP3.4
  N8: Part1.N$72, J3.pulse
  N9: Part1.N$87, J3.gnd
  N10: Part1.N$90, J3.Vcc
  N11: Part1.N$122, J9.pulse
  N12: Part1.N$165, J10.Vcc
  N13: Part1.N$177, J13.pulse
  N14: Part1.N$227, J14.pulse
  N15: Part1.N$229, J14.Vcc
  N16: Part1.N$231, J14.gnd
  N17: Part1.N$296, J5.Vcc
  N18: Part1.N$297, J5.pulse
  N19: Part1.N$299, J6.pulse
  N20: Part1.N$307, J12.gnd
  N21: Part1.N$309, J10.gnd
  N22: Part1.N$310, J11.gnd
  N23: Part1.N$311, J13.gnd
  N24: Part1.N$312, J13.Vcc
  N25: Part1.N$313, J12.Vcc
  N26: Part1.N$316, J5.gnd
  N27: Part1.N$317, J6.Vcc
  N28: Part1.N$318, J4.Vcc
  N29: Part1.N$319, J4.pulse
  N30: Part1.N$320, J8.Vcc
  N31: Part1.N$376, J6.gnd
  N32: Part1.N$377, J4.gnd
  N33: Part1.N$378, J9.gnd
  N34: Part1.N$379, J8.gnd
  N35: Part1.N$381, J9.Vcc
  N36: Part1.N$383, J8.pulse
  N37: Part1.N$400, J7.gnd
  N38: Part1.N$409, J7.pulse
  N39: Part1.N$410, J7.Vcc
  N40: Part1.N$411, J11.Vcc
  N41: Part1.N$412, J10.pulse
  N42: Part1.N$413, J11.pulse
  N43: Part1.N$414, J12.pulse
